// Logisim project Project2.circ as structural Verilog: 1 circuit, main circuit MIPS32
module MIPS32 (
);

  // OR_Gate or_1 is placed but not wired
  // RegisterFile registerfile_1: pin names not known
  // AND_Gate and_1 is placed but not wired
endmodule
